# Fritzing sketch Circuit (saved by Fritzing 0.9.3b)

parts:
  Part1 = Arduino Uno (Rev3)
  Module1 = Boladge HMC5883L Compass Module  # not connected
  HC-SR04_Sensor_1 = HC-SR04 Ultrasonic Distance Sensor  # not connected
  HC-SR04_Sensor_2 = HC-SR04 Ultrasonic Distance Sensor  # not connected
  HC-SR04_Sensor_3 = HC-SR04 Ultrasonic Distance Sensor  # not connected
  Part2 = Bluetooth HC-05 Macho  # not connected
  U1 = Vibration Motor- ROB-08449 [package=vibe-motor-10mm]
  U2 = Vibration Motor- ROB-08449 [package=vibe-motor-10mm]
  R1 = Resistor [tolerance=±5% resistance=220 package=THT]
  R2 = Resistor [tolerance=±5% resistance=220 package=THT]
  S1 = Momentary Switch [package=tactile-pth]
  R3 = Resistor [tolerance=±5% resistance=220 package=THT]

nets:
  N1: Part1.D9_PWM, U1.+
  N2: Part1.D10_PWM/SS, S1.3, R3.Pin_1
  N3: Part1.GND, R3.Pin_0
  N4: U1.-, R2.Pin_1
  N5: U2.-, R1.Pin_1

custom parts:
  Boladge HMC5883L Compass Module: Cheap digital compass module
